# Fritzing sketch HomeStstion (saved by Fritzing 0.9.4)
breadboards: 1

parts:
  Деталь1 = Arduino Uno (Rev3)
  T1 = LM35 Temperature Sensor [package="TO92 [THT]"]
  J1 = Piezo Speaker
  LCD1 = LCD screen  # not connected
  M1 = pcf8574 io expansion board [package=THT]
  IC1 = MQ-2 [package="DIP (Dual Inline) [THT]"]

nets:
  N1: Деталь1.A0, T1.Vout
  N2: Деталь1.A2, IC1.pin4
  N3: Деталь1.D11_PWM/MOSI, J1.pin2
  N4: Деталь1.A4/SDA, M1.SDA
  N5: Деталь1.A5/SCL, M1.SCL
  5V: Деталь1.5V, T1.+Vs, M1.VCC, IC1.pin1
  GND: Деталь1.GND, T1.GND, J1.pin1, M1.GND, IC1.pin2

custom parts:
  pcf8574 io expansion board: pcf8574 io expansion board.
  MQ-2: MQ-2 Gas Sensor module
